# Fritzing sketch diyDrumPads (saved by Fritzing 0.7.10b)
breadboards: 1

parts:
  IC1 = IC, DIP package, 20 pins [chip_label=IC]
  Nano1 = Arduino Nano v2.3
  R1 = Resistor [tolerance=±5% resistance=220 package=THT]
  XTAL1 = Crystal [frequency="16 Mhz" package=THT]
  CONN1 = USB connector [package=THT]

nets:
  N1: IC1.pin2, Nano1.D1TX
  N2: IC1.pin4, XTAL1.pin_0
  N3: IC1.pin5, XTAL1.pin_1
  N4: IC1.pin6, CONN1.d+
  N5: IC1.pin7, R1.Pin_0, CONN1.d-
  N6: IC1.pin10, CONN1.GND, CONN1.chassis5, CONN1.chassis6
  N7: IC1.pin20, Nano1.3V3
